# Fritzing sketch Feuermelder_client_circuit_diagram (saved by Fritzing 0.9.3b)
breadboards: 1

parts:
  Bauteil1 = Adafruit Feather HUZZAH ESP8266 [part_number="Adafruit #2821"]
  R3 = Resistor [tolerance=±5% resistance=1k package=THT]
  SG2 = Piezo [package=buzzer-12mm-ns-kit]
  LED1 = smd LED [color="Red (633nm)" package="1206 [SMD]"]

nets:
  N1: Bauteil1.GPIO13/MOSI, R3.Pin_0
  N2: Bauteil1.GND, SG2.2, LED1.cathode
  N3: R3.Pin_1, SG2.1, LED1.anode

custom parts:
  Adafruit Feather HUZZAH ESP8266: his is the Adafruit Feather HUZZAH ESP8266 - our take on an 'all-in-one' ESP8266 WiFi development board with built in USB and battery charging. Its an ESP8266 WiFi module with all the extras you need, ready to rock! We have other boards in the Feather family, check'em out here. At the Feather HUZZAH's heart is an ESP8266 WiFi microcontroller clocked at 80 MHz and at 3.3V logic. This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
  Piezo: Buzzer Spark Fun Electronics SIK for MicroView
