# Fritzing sketch Projekt_Haupt_Fritzing (saved by Fritzing 0.9.3b)
breadboards: 1

parts:
  Bauteil1 = Adafruit Feather HUZZAH ESP8266 [part_number="Adafruit #2821"]
  RHT2 = Humidity and Temperature Sensor RHT03
  R2 = Resistor [tolerance=±5% resistance=1k package=THT]
  R3 = Resistor [tolerance=±5% resistance=1k package=THT]

nets:
  N1: Bauteil1.GPIO13/MOSI, RHT2.Data-signal, R2.Pin_1
  N2: Bauteil1.GND, RHT2.GND_2, R3.Pin_0
  3.3V: Bauteil1.3.3V, RHT2.Vcc, R2.Pin_0

custom parts:
  Adafruit Feather HUZZAH ESP8266: his is the Adafruit Feather HUZZAH ESP8266 - our take on an 'all-in-one' ESP8266 WiFi development board with built in USB and battery charging. Its an ESP8266 WiFi module with all the extras you need, ready to rock! We have other boards in the Feather family, check'em out here. At the Feather HUZZAH's heart is an ESP8266 WiFi microcontroller clocked at 80 MHz and at 3.3V logic. This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
